// Logisim project 7 segment decoder chip.circ as structural Verilog: 11 circuits, main circuit main
module main (
  input  in_1,
  input  in_2,
  input  in_3,
  input  in_4,
  output A,
  output B,
  output C,
  output D,
  output E,
  output F,
  output G
);

  wire and_1_out, and_3_out, and_5_out, and_7_out, and_8_out, and_9_out, not_1_out;

  not not_1 (not_1_out, in_2);
  not not_2 (not_1_out, in_3);
  not not_3 (not_1_out, in_4);
  and and_1 (and_1_out, in_2, not_1_out);
  and and_2 (and_1_out, in_2, in_4);
  and and_3 (and_3_out, in_2, not_1_out);
  and and_4 (and_1_out, in_3, in_4);
  and and_5 (and_5_out, not_1_out, not_1_out);
  and and_6 (and_1_out, in_3, not_1_out);
  and and_7 (and_7_out, in_2, not_1_out, in_4);
  and and_8 (and_8_out, not_1_out, in_3);
  and and_9 (and_9_out, in_2, not_1_out);
  or or_1 (A, in_1, in_3, and_1_out, and_1_out);
  or or_2 (B, and_1_out, and_1_out, not_1_out);
  or or_3 (C, in_2, not_1_out, in_4);
  or or_4 (D, in_1, and_1_out, and_8_out, and_1_out, and_7_out);
  or or_5 (E, and_1_out, and_1_out);
  or or_6 (F, in_1, and_5_out, and_3_out, and_9_out);
  or or_7 (G, in_1, and_9_out, and_1_out, and_8_out);
  _7_Segment_Display u_7_segment_display_1 (.g(G), .f(F), .a(A), .b(B), .e(E), .d(D), .c(C));  // open: dp
endmodule

module A (
  input  a,
  input  b,
  input  c,
  input  d,
  output A_2
);

  wire and_1_out, and_2_out, not_1_out, not_2_out, or_1_out, or_2_out;

  not not_1 (not_1_out, b);
  and and_1 (and_1_out, not_1_out, not_2_out);
  not not_2 (not_2_out, d);
  and and_2 (and_2_out, b, d);
  or or_1 (or_1_out, and_1_out, c);
  or or_2 (or_2_out, and_2_out, a);
  or or_3 (A_2, or_1_out, or_2_out);
endmodule

module B (
  input  a,
  input  b,
  input  c,
  input  d,
  output B_2
);

  wire and_1_out, and_2_out, not_1_out, not_2_out, not_3_out;

  not not_1 (not_1_out, b);
  not not_2 (not_2_out, c);
  and and_1 (and_1_out, not_2_out, not_3_out);
  not not_3 (not_3_out, d);
  and and_2 (and_2_out, c, d);
  or or_1 (B_2, not_1_out, and_1_out, and_2_out);
endmodule

module C (
  input  a,
  input  b,
  input  c,
  input  d,
  output C_2
);

  wire not_1_out, or_1_out;

  not not_1 (not_1_out, c);
  or or_1 (or_1_out, not_1_out, d);
  or or_2 (C_2, or_1_out, b);
endmodule

module D (
  input  a,
  input  b,
  input  c,
  input  d,
  output D_2
);

  wire and_1_out, and_2_out, and_3_out, and_4_out, and_5_out, not_1_out, not_2_out, not_3_out, not_4_out,
       not_5_out, or_1_out, or_2_out, or_3_out;

  not not_1 (not_1_out, b);
  and and_1 (and_1_out, not_1_out, not_2_out);
  not not_2 (not_2_out, d);
  not not_3 (not_3_out, b);
  and and_2 (and_2_out, not_3_out, c);
  not not_4 (not_4_out, d);
  and and_3 (and_3_out, b, not_5_out);
  not not_5 (not_5_out, c);
  or or_1 (or_1_out, and_1_out, and_2_out);
  and and_4 (and_4_out, c, not_4_out);
  and and_5 (and_5_out, and_3_out, d);
  or or_2 (or_2_out, or_1_out, and_4_out);
  or or_3 (or_3_out, and_5_out, a);
  or or_4 (D_2, or_2_out, or_3_out);
endmodule

module E (
  input  a,
  input  b,
  input  c,
  input  d,
  output x
);

  wire and_1_out, and_2_out, and_3_out, not_1_out, not_2_out, not_3_out, not_4_out, not_5_out, not_6_out;

  not not_1 (not_1_out, b);
  not not_2 (not_2_out, c);
  and and_1 (and_1_out, not_1_out, not_2_out, not_3_out);
  not not_3 (not_3_out, d);
  not not_4 (not_4_out, a);
  and and_2 (and_2_out, not_4_out, c, not_5_out);
  not not_5 (not_5_out, d);
  and and_3 (and_3_out, a, b, not_6_out);
  not not_6 (not_6_out, c);
  or or_1 (x, and_1_out, and_2_out, and_3_out);
endmodule

module F (
  input  a,
  input  b,
  input  c,
  input  d,
  output x
);

  wire and_1_out, and_2_out, and_3_out, not_1_out, not_2_out, not_3_out, not_4_out, or_1_out, or_2_out;

  not not_1 (not_1_out, c);
  and and_1 (and_1_out, not_1_out, not_2_out);
  not not_2 (not_2_out, d);
  and and_2 (and_2_out, b, not_3_out);
  not not_3 (not_3_out, c);
  and and_3 (and_3_out, b, not_4_out);
  not not_4 (not_4_out, d);
  or or_1 (or_1_out, and_1_out, and_2_out);
  or or_2 (or_2_out, and_3_out, a);
  or or_3 (x, or_1_out, or_2_out);
endmodule

module G (
  input  a,
  input  b,
  input  c,
  input  d,
  output x
);

  wire and_1_out, and_2_out, and_3_out, not_1_out, not_2_out, not_3_out, or_1_out, or_2_out;

  not not_1 (not_1_out, b);
  and and_1 (and_1_out, not_1_out, c);
  and and_2 (and_2_out, b, not_2_out);
  not not_2 (not_2_out, c);
  and and_3 (and_3_out, b, not_3_out);
  not not_3 (not_3_out, d);
  or or_1 (or_1_out, and_1_out, and_2_out);
  or or_2 (or_2_out, and_3_out, a);
  or or_3 (x, or_1_out, or_2_out);
endmodule

module bcd (
  input  b,
  input  a,
  input  c,
  input  d,
  output A_2,
  output B_2,
  output C_2,
  output D_2,
  output E,
  output F,
  output G
);

  wire and_1_out, and_2_out, and_3_out, and_4_out, and_5_out, and_6_out, and_7_out, and_8_out, and_9_out,
       and_10_out, and_11_out, and_12_out, and_13_out, and_14_out, and_15_out, and_16_out, and_17_out,
       not_1_out, not_2_out, not_3_out, not_4_out, not_5_out, not_6_out, not_7_out, not_8_out, not_9_out,
       not_10_out, not_11_out, not_12_out, not_13_out, not_14_out, not_15_out, not_16_out, not_17_out,
       not_18_out, not_19_out, not_20_out, not_21_out, or_1_out, or_2_out, or_3_out, or_4_out, or_6_out,
       or_8_out, or_9_out, or_10_out, or_11_out, or_14_out, or_15_out;

  not not_1 (not_1_out, a);
  and and_1 (and_1_out, not_1_out, not_2_out);
  not not_2 (not_2_out, d);
  and and_2 (and_2_out, a, d);
  not not_3 (not_3_out, a);
  not not_4 (not_4_out, c);
  and and_3 (and_3_out, not_4_out, not_5_out);
  not not_5 (not_5_out, d);
  not not_6 (not_6_out, c);
  or or_1 (or_1_out, not_6_out, d);
  not not_7 (not_7_out, a);
  and and_4 (and_4_out, not_7_out, not_8_out);
  not not_8 (not_8_out, d);
  not not_9 (not_9_out, a);
  and and_5 (and_5_out, not_9_out, c);
  not not_10 (not_10_out, d);
  and and_6 (and_6_out, a, not_11_out);
  not not_11 (not_11_out, c);
  not not_12 (not_12_out, a);
  and and_7 (and_7_out, not_12_out, not_13_out);
  not not_13 (not_13_out, d);
  and and_8 (and_8_out, c, not_14_out);
  not not_14 (not_14_out, d);
  not not_15 (not_15_out, c);
  and and_9 (and_9_out, not_15_out, not_16_out);
  not not_16 (not_16_out, d);
  and and_10 (and_10_out, a, not_17_out);
  not not_17 (not_17_out, c);
  and and_11 (and_11_out, a, not_18_out);
  not not_18 (not_18_out, d);
  not not_19 (not_19_out, a);
  and and_12 (and_12_out, not_19_out, c);
  and and_13 (and_13_out, a, not_20_out);
  not not_20 (not_20_out, c);
  and and_14 (and_14_out, a, not_21_out);
  not not_21 (not_21_out, d);
  or or_2 (or_2_out, and_1_out, c);
  or or_3 (or_3_out, and_2_out, b);
  or or_4 (or_4_out, not_3_out, and_3_out);
  and and_15 (and_15_out, c, d);
  or or_5 (C_2, or_1_out, a);
  or or_6 (or_6_out, and_4_out, and_5_out);
  and and_16 (and_16_out, c, not_10_out);
  and and_17 (and_17_out, and_6_out, d);
  or or_7 (E, and_7_out, and_8_out);
  or or_8 (or_8_out, and_9_out, and_10_out);
  or or_9 (or_9_out, and_11_out, b);
  or or_10 (or_10_out, and_12_out, and_13_out);
  or or_11 (or_11_out, and_14_out, b);
  or or_12 (A_2, or_2_out, or_3_out);
  or or_13 (B_2, or_4_out, and_15_out);
  or or_14 (or_14_out, or_6_out, and_16_out);
  or or_15 (or_15_out, and_17_out, b);
  or or_16 (F, or_8_out, or_9_out);
  or or_17 (G, or_10_out, or_11_out);
  or or_18 (D_2, or_14_out, or_15_out);
endmodule

module BCD_2 (
  input  in_1,
  input  in_2,
  input  in_3,
  input  in_4,
  output out_5,
  output out_6,
  output out_7,
  output out_8,
  output out_9,
  output out_10,
  output out_11
);

  A a_1 (.a(in_1), .b(in_2), .c(in_3), .d(in_4), .A_2(out_5));
  B b_1 (.a(in_1), .B_2(out_6), .b(in_2), .c(in_3), .d(in_4));
  C c_1 (.a(in_1), .b(in_2), .c(in_3), .d(in_4), .C_2(out_7));
  D d_1 (.a(in_1), .b(in_2), .c(in_3), .d(in_4), .D_2(out_8));
  E e_1 (.a(in_1), .b(in_2), .c(in_3), .d(in_4), .x(out_9));
  F f_1 (.a(in_1), .b(in_2), .c(in_3), .d(in_4), .x(out_10));
  G g_1 (.a(in_1), .b(in_2), .c(in_3), .d(in_4), .x(out_11));
  _7_Segment_Display u_7_segment_display_1 (
    .g(out_11), .f(out_10), .a(out_5), .b(out_6), .e(out_9), .d(out_8), .c(out_7));  // open: dp
endmodule

module ti (
);

  BCD_2 bcd_2_1 ();  // open: in_1, in_2, in_3, in_4, out_5, out_6, out_7, out_8, out_9, out_10, out_11
endmodule
